# Fritzing sketch inplant-schematic (saved by Fritzing 0.9.3b)

parts:
  Part5 = Adafruit HUZZAH32 ESP32 Feather [part_number="Adafruit #3405"]
  Capacitive_Soil_Moisture_Sensor1 = DFRobot Capacitive Soil Moisture Sensor V1.0 [part_number=SEN0193]
  S1 = Toggle Switch [package=THT]
  U1 = LIPO-2000mAh [package=lipo-2000]

nets:
  N1: Part5.A1_DAC1, Capacitive_Soil_Moisture_Sensor1.A
  GND: Part5.GND, Capacitive_Soil_Moisture_Sensor1.GND
  3.3V: Part5.3.3V, Capacitive_Soil_Moisture_Sensor1.VCC
  N2: S1.L1, U1.+
  N3: S1.L2, U1.-

custom parts:
  DFRobot Capacitive Soil Moisture Sensor V1.0: DFRobot Capacitive Soil Moisture Sensor V1.0 This product measures soil moisture levels by capacitive sensing, rather than resistive sensing like other types of moisture sensor. It is made of a corrosion resistant material giving it a long service life. Insert it into soil and impress your friends with the real-time soil moisture data! The product includes an on-board voltage regulator which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
